# Fritzing sketch PCB revision B (saved by Fritzing 0.9.3b)
circuit board: 4.82cm x 2.54cm
breadboards: 1

parts:
  NODE_MCU = NodeMCU V1.0
  R_10KΩ = Resistor [tolerance=±5% resistance=10k package=THT]
  + = Header 1 [package=1x01_offset]
  - = Header 1 [package=1x01_offset]
  D = Header 1 [package=1x01_offset]
  BUZZER = Piezo Speaker - PC Mount [part_number=COM-07950]
  EC_1000uF = Electrolytic Capacitor [capacitance=1mF voltage=6.3V package="200 mil [THT, electrolytic]"]
  LDR = PHOTOCELL [package=photocell-kit]

nets:
  N1: NODE_MCU.D1, D.1
  N2: NODE_MCU.D2, BUZZER.VCC
  N3: NODE_MCU.3V3, +.1, EC_1000uF.+, LDR.P$1
  GND: NODE_MCU.GND, R_10KΩ.Pin_0, -.1, BUZZER.GND, EC_1000uF.-
  N4: NODE_MCU.A0, R_10KΩ.Pin_1, LDR.P$2

notes:
  PIXEL
  REV B

custom parts:
  NodeMCU V1.0: ESP8266 based NodeMCU
  Piezo Speaker - PC Mount: This is a small 12mm round speaker that operates around the audible 2kHz range. You can use these speakers to create simple music or user interfaces. Each speaker is PTH solderable and requires an operating voltage of 3.5-5V with a mean current of 35mA max. These speakers also have a typical sound output of 95 dBA and a coil resistance of 42 ±6.3 ohms.
